# Fritzing sketch LED&Buzzer Sketch&Mic&VibrationSensor (saved by Fritzing 0.9.3b)
breadboards: 1

parts:
  Part1 = Arduino Yun
  Grove1 = Grove Buzz
  LED1 = LED - 5mm [color="Red (633nm)" package="5 mm [THT]"]
  R1 = Resistor [tolerance=±5% resistance=220 package=THT]
  J1 = Piezo Speaker
  SW-1 = Vibration sensor module

nets:
  N1: Part1.A0, Grove1.SIG
  N2: Part1.D2, LED1.cathode
  N3: Part1.D3_PWM, J1.pin2
  N4: Part1.D4, SW-1.Digital_output
  VCC: Part1.5V, Grove1.VCC, SW-1.vcc
  GND: Part1.GND, Grove1.GND, R1.Pin_1, J1.pin1, SW-1.Ground
  N5: LED1.anode, R1.Pin_0

custom parts:
  Vibration sensor module: Single-roller type full induction trigger switch. When no vibration or tilt, the product is ON conduction state, and in the steady state, when a vibration or tilt, the switch will be rendered instantly disconnect the conductive resistance increases, generating a current pulse signal, thereby triggering circuit. The default state of the swith is close Digital output Supply voltage:3.3V-5V On-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
