# Fritzing sketch arduinoBabyMonitor_LMG (saved by Fritzing 0.9.3b)

parts:
  Part1 = Arduino Yun
  Movment_Sensor = Rotary Potentiometer (Small) [maximum_resistance=100kΩ package=THT]
  Temperature_Sensor = Grove Temperature Sensor
  ON_Button = Grove Button
  CONN1 = USB connector [package=THT]

nets:
  N1: Part1.D8, Movment_Sensor.leg1
  N2: Part1.D2, ON_Button.NC
  N3: Part1.D4, Temperature_Sensor.VCC
  N4: Part1.3V3, CONN1.d-

notes:
  TO-DO:
  - connect movement sensor to cot
  -Insert Sound sensor
  - Insert LED
  - Insert playback device for lullaby
  -
