# Fritzing sketch LED&Buzzer Sketch&Mic&VibrationSensor-UPDATED (saved by Fritzing 0.9.3b)
breadboards: 1

parts:
  Part1 = Arduino Yun
  Grove1 = Grove Buzz
  LED1 = LED - 5mm [color="Red (633nm)" package="5 mm [THT]"]
  R1 = Resistor [tolerance=±5% resistance=220 package=THT]
  J1 = Piezo Speaker  # not connected
  SW-1 = Vibration sensor module
  J2 = Piezo Speaker
  Q1 = NPN-Transistor [package="TO92 [THT]"]

nets:
  VCC: Part1.5V, Grove1.VCC, SW-1.vcc, J2.pin1
  N1: Part1.D9_PWM, SW-1.Digital_output
  N2: Part1.D10_PWM/SS, LED1.anode, R1.Pin_1
  N3: Part1.D11_PWM/MOSI, Q1.B
  GND: Part1.GND, Grove1.GND, LED1.cathode, R1.Pin_0, SW-1.Ground, Q1.C
  N4: J2.pin2, Q1.E

custom parts:
  Vibration sensor module: Single-roller type full induction trigger switch. When no vibration or tilt, the product is ON conduction state, and in the steady state, when a vibration or tilt, the switch will be rendered instantly disconnect the conductive resistance increases, generating a current pulse signal, thereby triggering circuit. The default state of the swith is close Digital output Supply voltage:3.3V-5V On-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
