# Fritzing sketch LED&Buzzer Sketch&Mic (saved by Fritzing 0.9.3b)
breadboards: 1

parts:
  Part1 = Arduino Yun
  Grove1 = Grove Buzz
  LED1 = LED - 5mm [color="Red (633nm)" package="5 mm [THT]"]
  R1 = Resistor [tolerance=±5% resistance=220 package=THT]
  J1 = Piezo Speaker

nets:
  N1: Part1.A0, Grove1.SIG
  N2: Part1.D2, LED1.cathode
  N3: Part1.D3_PWM, J1.pin2
  5V: Part1.5V, Grove1.VCC
  GND: Part1.GND, Grove1.GND, R1.Pin_1, J1.pin1
  N4: LED1.anode, R1.Pin_0
